# Fritzing sketch protoboard layout (saved by Fritzing 0.9.2b)

parts:
  Part2 = Logic Level Converter Bi-Directional BOB-12009
  U1 = ESP8266 WiFi Module [part_number=ESP8266]
  R1 = Resistor [tolerance=±5% resistance=10k package="0603 [SMD]"]
  AM1 = AM2302 Humidity and Temperature Sensor  # not connected
  R2 = Resistor [tolerance=±5% resistance=10k package="0603 [SMD]"]
  C1 = Capacitor Polarized [package=cpol-radial-10uf-25v]
  R3 = Resistor [tolerance=±5% resistance=10k package="0603 [SMD]"]
  R4 = Resistor [tolerance=±5% resistance=10k package="0603 [SMD]"]
  R5 = Resistor [tolerance=±5% resistance=10k package="0603 [SMD]"]
  LED1 = RGB LED (com. cathode, rbg) [package="5 mm [THT]"]
  R6 = Resistor [tolerance=±5% resistance=270 package="0805 [SMD]"]
  R7 = Resistor [tolerance=±5% resistance=270 package="0805 [SMD]"]
  R8 = Resistor [tolerance=±5% resistance=270 package="0805 [SMD]"]
  Part3 = Arduino Prototyping Shield
  R9 = Resistor [tolerance=±5% resistance=10k package="0603 [SMD]"]
  C3 = Electrolytic Capacitor [capacitance=0.47mF package="1010 [SMD, electrolytic]"]
  IC1 = Voltage Regulator AMS1117 [package=sot223]

nets:
  N1: Part2.LV4, Part3.N$269
  N2: Part2.LV3, Part3.N$307
  N3: Part2.GND, Part3.N$313, Part3.N$408
  N4: Part2.LV, Part3.N$414
  N5: Part2.LV2, Part3.N$419
  N6: Part2.LV1, Part3.N$433
  N7: Part2.HV1, Part3.N$429
  N8: Part2.HV2, Part3.N$423
  N9: Part2.HV, Part3.N$407
  N10: Part2.HV3, Part3.N$153
  N11: Part2.HV4, Part3.N$395
  N12: U1.RXD, Part3.N$96
  N13: U1.VCC, Part3.N$192
  N14: U1.GPIO_0, Part3.N$91
  N15: U1.GPIO_16, Part3.N$180
  N16: U1.GPIO_2, Part3.N$89
  N17: U1.CH_PD, Part3.N$168
  N18: U1.GND, Part3.N$88
  N19: U1.TXD, Part3.N$156
  N20: R1.Pin_0, Part3.N$399
  N21: R1.Pin_1, Part3.N$428
  N22: R2.Pin_0, Part3.N$167
  N23: R2.Pin_1, Part3.N$238
  N24: C1.+, Part3.N$378
  N25: C1.-, Part3.N$381
  N26: R3.Pin_0, Part3.N$179
  N27: R3.Pin_1, Part3.N$242
  N28: R4.Pin_0, Part3.N$191
  N29: R4.Pin_1, Part3.N$416
  N30: R5.Pin_0, Part3.N$203
  N31: R5.Pin_1, Part3.N$201
  N32: LED1.red_anode, R8.Pin_0, Part3.N$48, Part3.N$49
  N33: LED1.common_cathode, Part3.GND, C3.-
  N34: LED1.blue_anode, R6.Pin_0, Part3.N$72, Part3.N$73
  N35: LED1.green_anode, R7.Pin_0, Part3.N$85, Part3.N$86
  N36: R6.Pin_1, Part3.N$279
  N37: R7.Pin_1, Part3.N$280
  N38: R8.Pin_1, Part3.N$286
  N39: Part3.+5V, C3.+
  N40: Part3.N$155, R9.Pin_0
  N41: Part3.N$237, R9.Pin_1
  N42: Part3.N$261, Part3.N$360, IC1.OUT
  N43: Part3.N$262, IC1.IN
  N44: Part3.N$290, IC1.GND

notes:
  12/13 for Serial Output

custom parts:
  Logic Level Converter Bi-Directional BOB-12009: SparkFun product BOB-12009 If you’ve ever tried to connect a 3.3V device to a 5V system, you know what a challenge it can be. The SparkFun bi-directional logic level converter is a small device that safely steps down 5V signals to 3.3V AND steps up 3.3V to 5V at the same time. This level converter also works with 2.8V and 1.8V devices. What really separates this Logic level converter from our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
  ESP8266 WiFi Module: Generic WiFi Module based on the ESP8266 with onboard PCB antenna and UART communications
